// Logisim project proj.circ as structural Verilog: 10 circuits, main circuit main
module main (
);

  wire clock_1_out, counter_1_carry, left, right, startGame_out;
  wire [3:0] map_1_score1, map_1_score2, map_1_score3;
  wire [6:0] keyboard_1_data;
  wire [23:0] map_1_out_4, map_1_out_5, map_1_out_6, map_1_out_7, map_1_out_8, map_1_out_9, map_1_out_10,
       map_1_out_11, map_1_out_12, map_1_out_16, map_1_out_17, map_1_out_18, map_1_out_19, map_1_out_20,
       map_1_out_21, map_1_out_22, map_1_out_23, map_1_out_24, map_1_out_25, map_1_out_26, map_1_out_27,
       map_1_out_28, map_1_out_29, map_1_out_30, map_1_out_31, map_1_out_32, map_1_out_33, map_1_out_34,
       map_1_out_35, map_1_out_36, map_1_out_37, map_1_out_38;

  Hex_Digit_Display hex_digit_display_1 (.value(map_1_score3));  // open: dp
  Hex_Digit_Display hex_digit_display_2 (.value(map_1_score2));  // open: dp
  map map_1 (
    .loadStartField(startGame_out), .in_2(left), .in_3(right), .score3(map_1_score3), .score2(map_1_score2),
    .score1(map_1_score1), .out_4(map_1_out_4), .out_5(map_1_out_5), .out_6(map_1_out_6),
    .out_7(map_1_out_7), .out_8(map_1_out_8), .out_9(map_1_out_9), .out_10(map_1_out_10),
    .out_11(map_1_out_11), .out_12(map_1_out_12), .out_16(map_1_out_16), .out_17(map_1_out_17),
    .out_18(map_1_out_18), .out_19(map_1_out_19), .out_20(map_1_out_20), .out_21(map_1_out_21),
    .out_22(map_1_out_22), .out_23(map_1_out_23), .out_24(map_1_out_24), .out_25(map_1_out_25),
    .out_26(map_1_out_26), .out_27(map_1_out_27), .out_28(map_1_out_28), .out_29(map_1_out_29),
    .out_30(map_1_out_30), .out_31(map_1_out_31), .out_32(map_1_out_32), .out_33(map_1_out_33),
    .out_34(map_1_out_34), .out_35(map_1_out_35), .out_36(map_1_out_36), .out_37(map_1_out_37),
    .out_38(map_1_out_38));
  DotMatrix #(.inputtype("row"), .matrixcols(24), .matrixrows(32)) dotmatrix_1 (
    .row0(map_1_out_4), .row1(map_1_out_5), .row2(map_1_out_6), .row3(map_1_out_7), .row4(map_1_out_8),
    .row5(map_1_out_9), .row6(map_1_out_10), .row7(map_1_out_11), .row8(map_1_out_12), .row9(map_1_out_16),
    .row10(map_1_out_17), .row11(map_1_out_18), .row12(map_1_out_19), .row13(map_1_out_20),
    .row14(map_1_out_21), .row15(map_1_out_22), .row16(map_1_out_23), .row17(map_1_out_24),
    .row18(map_1_out_25), .row19(map_1_out_26), .row20(map_1_out_27), .row21(map_1_out_28),
    .row22(map_1_out_29), .row23(map_1_out_30), .row24(map_1_out_31), .row25(map_1_out_32),
    .row26(map_1_out_33), .row27(map_1_out_34), .row28(map_1_out_35), .row29(map_1_out_36),
    .row30(map_1_out_37), .row31(map_1_out_38));
  Button startGame (.out(startGame_out));
  Hex_Digit_Display hex_digit_display_3 (.value(map_1_score1));  // open: dp
  Counter #(.width(5), .max('h1f)) counter_1 (
    .carry(counter_1_carry), .clk(clock_1_out));  // open: load, D, count, Q, clr
  Clock clock_1 (.out(clock_1_out));
  Keyboard keyboard_1 (.clk(counter_1_carry), .clr(counter_1_carry), .data(keyboard_1_data));  // open: re, avail
  // Probe on keyboard_1_data
  Comparator #(.width(7)) comparator_1 (.a(7'b1100001), .b(keyboard_1_data), .eq(left));  // open: gt, lt
  Comparator #(.width(7)) comparator_2 (.a(keyboard_1_data), .b(7'b1100100), .eq(right));  // open: gt, lt
endmodule

module map (
  input  loadStartField,
  input  in_2,
  input  in_3,
  output [23:0] out_4,
  output [23:0] out_5,
  output [23:0] out_6,
  output [23:0] out_7,
  output [23:0] out_8,
  output [23:0] out_9,
  output [23:0] out_10,
  output [23:0] out_11,
  output [23:0] out_12,
  output [3:0] score3,
  output [3:0] score2,
  output [3:0] score1,
  output [23:0] out_16,
  output [23:0] out_17,
  output [23:0] out_18,
  output [23:0] out_19,
  output [23:0] out_20,
  output [23:0] out_21,
  output [23:0] out_22,
  output [23:0] out_23,
  output [23:0] out_24,
  output [23:0] out_25,
  output [23:0] out_26,
  output [23:0] out_27,
  output [23:0] out_28,
  output [23:0] out_29,
  output [23:0] out_30,
  output [23:0] out_31,
  output [23:0] out_32,
  output [23:0] out_33,
  output [23:0] out_34,
  output [23:0] out_35,
  output [23:0] out_36,
  output [23:0] out_37,
  output [23:0] out_38
);

  wire and_1_out, buffer_1_out, buffer_2_out, buffer_3_out, buffer_4_out, clock, clock_1_out, clock_2_out,
       collision, controlled_buffer_1_out, controlled_buffer_2_out, controlled_buffer_4_out, counter_9_carry,
       counter_10_carry, \end , fst, Jump, load, nor_1_out, not_1_out, not_2_out, or_1_out, or_2_out,
       or_3_out, or_4_out, pull_resistor_3_node, snd, up;
  wire [1:0] counter_3_q;
  wire [4:0] counter_1_q, counter_2_q, counter_7_q, counter_8_q, getrandom_1_bus_0, rowPos;
  wire [7:0] r1, r2;
  wire [23:0] char, multiplexer_1_out, row0, row1, row2, row3, row4, row5, row6, row7, row8, row9, row10,
       row11, row12, row13, row14, row15, row16, row17, row18, row19, row20, row21, row22, row23, row24,
       row25, row26, row27, row28, row29, row30, row31, shifter_1_out, shifter_2_out, startgamefield_1_out_1,
       startgamefield_1_out_2, startgamefield_1_out_3, startgamefield_1_out_4, startgamefield_1_out_5,
       startgamefield_1_out_6, startgamefield_1_out_7, startgamefield_1_out_8, startgamefield_1_out_9,
       startgamefield_1_out_10, startgamefield_1_out_11, startgamefield_1_out_12, startgamefield_1_out_13,
       startgamefield_1_out_14, startgamefield_1_out_15, startgamefield_1_out_16, startgamefield_1_out_17,
       startgamefield_1_out_18, startgamefield_1_out_19, startgamefield_1_out_20, startgamefield_1_out_21,
       startgamefield_1_out_22, startgamefield_1_out_23, startgamefield_1_out_24, startgamefield_1_out_25,
       startgamefield_1_out_26, startgamefield_1_out_27, startgamefield_1_out_28, startgamefield_1_out_29,
       startgamefield_1_out_30, startgamefield_1_out_31, startgamefield_1_out_32, str0, str1, str2, str3,
       str4, str5, str6, str7, str8, str9, str10, str11, str12, str13, str14, str15, str16, str17, str18,
       str19, str20, str21, str22, str23, str24, str25, str26, str27, str28, str29, str30, str31;

  Clock clock_1 (.out(clock_1_out));
  getRandom getrandom_1 (.clock(clock_1_out), .bus_0(getrandom_1_bus_0));
  movement movement_1 (.movement(r2), .collision(Jump), .clock(clock), .isMoving(fst));
  Counter #(.width(5), .max('h17)) counter_1 (
    .D({5{1'b0}}), .Q(counter_1_q), .clk(in_2), .clr(load));  // open: load, count, carry
  Counter #(.width(5), .max('h17)) counter_2 (.Q(counter_2_q), .clk(in_3), .clr(load));  // open: load, D, count, carry
  or or_1 (or_1_out, loadStartField, \end );
  Shifter #(.width(24)) shifter_1 (.in(24'hf), .\dist (getrandom_1_bus_0), .out(shifter_1_out));
  Counter #(.width(2), .max('h3)) counter_3 (
    .Q(counter_3_q), .clk(controlled_buffer_1_out));  // open: load, D, count, carry, clr
  assign controlled_buffer_1_out = fst ? clock : 1'bz;  // Controlled_Buffer controlled_buffer_1
  Counter #(.width(1), .max('h1)) counter_4 (.carry(load), .clk(or_1_out));  // open: load, D, count, Q, clr
  Multiplexer #(.select(2), .width(24), .enable("false")) multiplexer_1 (
    .in0(shifter_1_out), .in1({24{1'b0}}), .in2(shifter_1_out), .in3({24{1'b0}}), .out(multiplexer_1_out),
    .sel(counter_3_q));
  Demultiplexer #(.select(5), .width(24), .enable("false")) demultiplexer_1 (
    .out0(row0), .out1(row1), .out2(row2), .out3(row3), .out4(row4), .out5(row5), .out6(row6), .out7(row7),
    .out8(row8), .out9(row9), .out10(row10), .out11(row11), .out12(row12), .out13(row13), .out14(row14),
    .out15(row15), .out16(row16), .out17(row17), .out18(row18), .out19(row19), .out20(row20), .out21(row21),
    .out22(row22), .out23(row23), .out24(row24), .out25(row25), .out26(row26), .out27(row27), .out28(row28),
    .out29(row29), .out30(row30), .out31(row31), .in(char), .sel(rowPos));
  Shifter #(.width(24), .shift("rl")) shifter_2 (.in(24'h1400), .\dist (counter_1_q), .out(shifter_2_out));
  Shift_Register #(.width(24), .length(32)) shiftRegister (
    .shift(1'b1), .in(multiplexer_1_out), .clk(or_2_out), .load(load), .d0(startgamefield_1_out_32),
    .q0(str31), .d1(startgamefield_1_out_31), .q1(str30), .d2(startgamefield_1_out_30), .q2(str29),
    .d3(startgamefield_1_out_29), .q3(str28), .d4(startgamefield_1_out_28), .q4(str27),
    .d5(startgamefield_1_out_27), .q5(str26), .d6(startgamefield_1_out_26), .q6(str25),
    .d7(startgamefield_1_out_25), .q7(str24), .d8(startgamefield_1_out_24), .q8(str23),
    .d9(startgamefield_1_out_23), .q9(str22), .d10(startgamefield_1_out_22), .q10(str21),
    .d11(startgamefield_1_out_21), .q11(str20), .d12(startgamefield_1_out_20), .q12(str19),
    .d13(startgamefield_1_out_19), .q13(str18), .d14(startgamefield_1_out_18), .q14(str17),
    .d15(startgamefield_1_out_17), .q15(str16), .d16(startgamefield_1_out_16), .q16(str15),
    .d17(startgamefield_1_out_15), .q17(str14), .d18(startgamefield_1_out_14), .q18(str13),
    .d19(startgamefield_1_out_13), .q19(str12), .d20(startgamefield_1_out_12), .q20(str11),
    .d21(startgamefield_1_out_11), .q21(str10), .d22(startgamefield_1_out_10), .q22(str9),
    .d23(startgamefield_1_out_9), .q23(str8), .d24(startgamefield_1_out_8), .q24(str7),
    .d25(startgamefield_1_out_7), .q25(str6), .d26(startgamefield_1_out_6), .q26(str5),
    .d27(startgamefield_1_out_5), .q27(str4), .d28(startgamefield_1_out_4), .q28(str3),
    .d29(startgamefield_1_out_3), .q29(str2), .d30(startgamefield_1_out_2), .q30(str1),
    .d31(startgamefield_1_out_1), .q31(str0));  // open: out, clr
  or or_2 (or_2_out, load, controlled_buffer_1_out);
  Pull_Resistor pull_resistor_1 (.node(controlled_buffer_1_out));
  Shifter #(.width(24), .shift("rr")) shifter_3 (.in(shifter_2_out), .\dist (counter_2_q), .out(char));
  Clock clock_2 (.out(clock_2_out));
  Counter #(.width(6), .max('h3f)) counter_5 (.carry(clock), .clk(clock_2_out));  // open: load, D, count, Q, clr
  startGameField startgamefield_1 (
    .out_1(startgamefield_1_out_1), .out_2(startgamefield_1_out_2), .out_3(startgamefield_1_out_3),
    .out_4(startgamefield_1_out_4), .out_5(startgamefield_1_out_5), .out_6(startgamefield_1_out_6),
    .out_7(startgamefield_1_out_7), .out_8(startgamefield_1_out_8), .out_9(startgamefield_1_out_9),
    .out_10(startgamefield_1_out_10), .out_11(startgamefield_1_out_11), .out_12(startgamefield_1_out_12),
    .out_13(startgamefield_1_out_13), .out_14(startgamefield_1_out_14), .out_15(startgamefield_1_out_15),
    .out_16(startgamefield_1_out_16), .out_17(startgamefield_1_out_17), .out_18(startgamefield_1_out_18),
    .out_19(startgamefield_1_out_19), .out_20(startgamefield_1_out_20), .out_21(startgamefield_1_out_21),
    .out_22(startgamefield_1_out_22), .out_23(startgamefield_1_out_23), .out_24(startgamefield_1_out_24),
    .out_25(startgamefield_1_out_25), .out_26(startgamefield_1_out_26), .out_27(startgamefield_1_out_27),
    .out_28(startgamefield_1_out_28), .out_29(startgamefield_1_out_29), .out_30(startgamefield_1_out_30),
    .out_31(startgamefield_1_out_31), .out_32(startgamefield_1_out_32));
  not not_1 (not_1_out, fst);
  and and_1 (and_1_out, not_1_out, snd);
  movement movement_2 (.movement(r1), .collision(and_1_out), .clock(clock), .isMoving(up));
  movement movement_3 (.movement(8'h7), .collision(Jump), .clock(clock), .isMoving(snd));
  not not_2 (not_2_out, load);
  or or_3 (or_3_out, up, load);
  assign controlled_buffer_2_out = or_3_out ? clock : 1'bz;  // Controlled_Buffer controlled_buffer_2
  Pull_Resistor pull_resistor_2 (.node(controlled_buffer_2_out));
  Pull_Resistor pull_resistor_3 (.node(pull_resistor_3_node));
  assign pull_resistor_3_node = nor_1_out ? clock : 1'bz;  // Controlled_Buffer controlled_buffer_3
  nor nor_1 (nor_1_out, snd, fst, collision, up);
  Counter #(.width(4), .max('h9)) counter_6 (
    .Q(score3), .clk(counter_9_carry), .clr(load));  // open: load, D, count, carry
  checkCollision checkcollision_1 (
    .str0(str31), .str1(str30), .str2(str29), .str3(str28), .str4(str27), .str5(str26), .str6(str25),
    .str7(str24), .str8(str23), .str9(str22), .str10(str21), .str11(str20), .str12(str19), .str13(str18),
    .str14(str17), .str15(str16), .str16(str15), .str17(str14), .str18(str13), .str19(str12), .str20(str11),
    .str21(str10), .str22(str9), .str23(str8), .str24(str7), .str25(str6), .str26(str5), .str27(str4),
    .str28(str3), .str29(str2), .str30(str1), .str31(str0), .rowPos(rowPos), .char(char), .out(collision));
  Counter #(.width(5), .max('h1f)) counter_7 (
    .load(load), .D(5'b00101), .count(not_2_out), .Q(counter_7_q), .clk(controlled_buffer_2_out));  // open: carry, clr
  Counter #(.width(5), .max('h1f), .trigger("falling")) counter_8 (
    .Q(counter_8_q), .clk(pull_resistor_3_node), .clr(load));  // open: load, D, count, carry
  Counter #(.width(4), .max('h9)) counter_9 (
    .Q(score2), .carry(counter_9_carry), .clk(counter_10_carry), .clr(load));  // open: load, D, count
  Subtractor #(.width(5)) subtractor_1 (.a(counter_7_q), .b(counter_8_q), .out(rowPos));  // open: bin, bout
  buf buffer_1 (buffer_1_out, buffer_2_out);
  buf buffer_2 (buffer_2_out, buffer_3_out);
  buf buffer_3 (buffer_3_out, load);
  Counter #(.width(4), .max('h9)) counter_10 (
    .Q(score1), .carry(counter_10_carry), .clk(controlled_buffer_4_out), .clr(load));  // open: load, D, count
  assign controlled_buffer_4_out = fst ? clock : 1'bz;  // Controlled_Buffer controlled_buffer_4
  Pull_Resistor pull_resistor_4 (.node(controlled_buffer_4_out));
  Comparator #(.width(5)) comparator_1 (.a(rowPos), .b({5{1'b1}}), .eq(\end ));  // open: gt, lt
  and and_2 (Jump, ~nor_1_out, ~snd, collision);  // AND_Gate
  buf buffer_4 (buffer_4_out, buffer_1_out);
  or or_4 (or_4_out, buffer_4_out, Jump);
  // Probe on r2
  processor processor_1 (.jumpInter(or_4_out), .rowPos(rowPos), .r2(r2), .r1(r1));
  // Probe on r1
  assign out_4 = str31 | row31;  // OR_Gate or_5, 24 bits wide
  assign out_5 = str30 | row30;  // OR_Gate or_6, 24 bits wide
  assign out_6 = str29 | row29;  // OR_Gate or_7, 24 bits wide
  assign out_7 = str28 | row28;  // OR_Gate or_8, 24 bits wide
  assign out_8 = str27 | row27;  // OR_Gate or_9, 24 bits wide
  assign out_9 = str26 | row26;  // OR_Gate or_10, 24 bits wide
  assign out_10 = str25 | row25;  // OR_Gate or_11, 24 bits wide
  assign out_11 = str24 | row24;  // OR_Gate or_12, 24 bits wide
  assign out_12 = str23 | row23;  // OR_Gate or_13, 24 bits wide
  assign out_16 = str22 | row22;  // OR_Gate or_14, 24 bits wide
  assign out_17 = str21 | row21;  // OR_Gate or_15, 24 bits wide
  assign out_18 = str20 | row20;  // OR_Gate or_16, 24 bits wide
  assign out_19 = str19 | row19;  // OR_Gate or_17, 24 bits wide
  assign out_20 = str18 | row18;  // OR_Gate or_18, 24 bits wide
  assign out_21 = str17 | row17;  // OR_Gate or_19, 24 bits wide
  assign out_22 = str16 | row16;  // OR_Gate or_20, 24 bits wide
  assign out_23 = str15 | row15;  // OR_Gate or_21, 24 bits wide
  assign out_24 = str14 | row14;  // OR_Gate or_22, 24 bits wide
  assign out_25 = str13 | row13;  // OR_Gate or_23, 24 bits wide
  assign out_26 = str12 | row12;  // OR_Gate or_24, 24 bits wide
  assign out_27 = str11 | row11;  // OR_Gate or_25, 24 bits wide
  assign out_28 = str10 | row10;  // OR_Gate or_26, 24 bits wide
  assign out_29 = str9 | row9;  // OR_Gate or_27, 24 bits wide
  assign out_30 = str8 | row8;  // OR_Gate or_28, 24 bits wide
  assign out_31 = str7 | row7;  // OR_Gate or_29, 24 bits wide
  assign out_32 = str6 | row6;  // OR_Gate or_30, 24 bits wide
  assign out_33 = str5 | row5;  // OR_Gate or_31, 24 bits wide
  assign out_34 = str4 | row4;  // OR_Gate or_32, 24 bits wide
  assign out_35 = str3 | row3;  // OR_Gate or_33, 24 bits wide
  assign out_36 = str2 | row2;  // OR_Gate or_34, 24 bits wide
  assign out_37 = str1 | row1;  // OR_Gate or_35, 24 bits wide
  assign out_38 = str0 | row0;  // OR_Gate or_36, 24 bits wide
endmodule

module checkCollision (
  input  [4:0] rowPos,
  input  [23:0] char,
  input  [23:0] str0,
  input  [23:0] str1,
  input  [23:0] str2,
  input  [23:0] str3,
  input  [23:0] str4,
  input  [23:0] str5,
  input  [23:0] str6,
  input  [23:0] str7,
  input  [23:0] str8,
  input  [23:0] str9,
  input  [23:0] str10,
  input  [23:0] str11,
  input  [23:0] str12,
  input  [23:0] str13,
  input  [23:0] str14,
  input  [23:0] str15,
  input  [23:0] str16,
  input  [23:0] str17,
  input  [23:0] str18,
  input  [23:0] str19,
  input  [23:0] str20,
  input  [23:0] str21,
  input  [23:0] str22,
  input  [23:0] str23,
  input  [23:0] str24,
  input  [23:0] str25,
  input  [23:0] str26,
  input  [23:0] str27,
  input  [23:0] str28,
  input  [23:0] str29,
  input  [23:0] str30,
  input  [23:0] str31,
  output out
);

  wire [23:0] and_1_out, multiplexer_1_out;

  Multiplexer #(.select(5), .width(24), .disabled(0), .enable("false")) multiplexer_1 (
    .in0({24{1'b0}}), .in1(str31), .in2(str30), .in3(str29), .in4(str28), .in5(str27), .in6(str26),
    .in7(str25), .in8(str24), .in9(str23), .in10(str22), .in11(str21), .in12(str20), .in13(str19),
    .in14(str18), .in15(str17), .in16(str16), .in17(str15), .in18(str14), .in19(str13), .in20(str12),
    .in21(str11), .in22(str10), .in23(str9), .in24(str8), .in25(str7), .in26(str6), .in27(str5), .in28(str4),
    .in29(str3), .in30(str2), .in31(str1), .out(multiplexer_1_out), .sel(rowPos));
  // Probe on char
  // Probe on multiplexer_1_out
  assign and_1_out = multiplexer_1_out & char;  // AND_Gate and_1, 24 bits wide
  or or_1 (out, and_1_out[0], and_1_out[1], and_1_out[2], and_1_out[3], and_1_out[4], and_1_out[5], and_1_out[6], and_1_out[7], and_1_out[8], and_1_out[9], and_1_out[10], and_1_out[11], and_1_out[12], and_1_out[13], and_1_out[14], and_1_out[15], and_1_out[16], and_1_out[17], and_1_out[18], and_1_out[19], and_1_out[20], and_1_out[21], and_1_out[22], and_1_out[23]);

  // Other names for the same wires on the sheet: str0_t[23:0] = str31; str1_t[23:0] = str30; str2_t[23:0] = str29;
  //   str3_t[23:0] = str28; str4_t[23:0] = str27; str5_t[23:0] = str26; str6_t[23:0] = str25; str7_t[23:0] = str24;
  //   str8_t[23:0] = str23; str9_t[23:0] = str22; str10_t[23:0] = str21; str11_t[23:0] = str20; str12_t[23:0] = str19;
  //   str13_t[23:0] = str18; str14_t[23:0] = str17; str15_t[23:0] = str16; str16_t[23:0] = str15;
  //   str17_t[23:0] = str14; str18_t[23:0] = str13; str19_t[23:0] = str12; str20_t[23:0] = str11;
  //   str21_t[23:0] = str10; str22_t[23:0] = str9; str23_t[23:0] = str8; str24_t[23:0] = str7; str25_t[23:0] = str6;
  //   str26_t[23:0] = str5; str27_t[23:0] = str4; str28_t[23:0] = str3; str29_t[23:0] = str2; str30_t[23:0] = str1;
  //   str31_t[23:0] = str0
endmodule

// OR
module _5BitOr (
  input  [4:0] num,
  output out
);

  or or_1 (out, num[0], num[1], num[2], num[3], num[4]);
endmodule

module startGameField (
  output [23:0] out_1,
  output [23:0] out_2,
  output [23:0] out_3,
  output [23:0] out_4,
  output [23:0] out_5,
  output [23:0] out_6,
  output [23:0] out_7,
  output [23:0] out_8,
  output [23:0] out_9,
  output [23:0] out_10,
  output [23:0] out_11,
  output [23:0] out_12,
  output [23:0] out_13,
  output [23:0] out_14,
  output [23:0] out_15,
  output [23:0] out_16,
  output [23:0] out_17,
  output [23:0] out_18,
  output [23:0] out_19,
  output [23:0] out_20,
  output [23:0] out_21,
  output [23:0] out_22,
  output [23:0] out_23,
  output [23:0] out_24,
  output [23:0] out_25,
  output [23:0] out_26,
  output [23:0] out_27,
  output [23:0] out_28,
  output [23:0] out_29,
  output [23:0] out_30,
  output [23:0] out_31,
  output [23:0] out_32
);


  assign out_1 = {24{1'b0}};
  assign out_2 = {24{1'b0}};
  assign out_3 = 24'h3c00;
  assign out_4 = {24{1'b0}};
  assign out_5 = {24{1'b0}};
  assign out_6 = {24{1'b0}};
  assign out_7 = 24'he00000;
  assign out_8 = {24{1'b0}};
  assign out_9 = {24{1'b0}};
  assign out_10 = {24{1'b0}};
  assign out_11 = 24'he00000;
  assign out_12 = {24{1'b0}};
  assign out_13 = {24{1'b0}};
  assign out_14 = {24{1'b0}};
  assign out_15 = 24'he00000;
  assign out_16 = {24{1'b0}};
  assign out_17 = {24{1'b0}};
  assign out_18 = {24{1'b0}};
  assign out_19 = 24'he00000;
  assign out_20 = {24{1'b0}};
  assign out_21 = {24{1'b0}};
  assign out_22 = {24{1'b0}};
  assign out_23 = 24'he00000;
  assign out_24 = {24{1'b0}};
  assign out_25 = {24{1'b0}};
  assign out_26 = {24{1'b0}};
  assign out_27 = 24'he00000;
  assign out_28 = {24{1'b0}};
  assign out_29 = {24{1'b0}};
  assign out_30 = {24{1'b0}};
  assign out_31 = 24'he00000;
  assign out_32 = {24{1'b0}};
endmodule

// CPU
module processor (
  input  jumpInter,
  input  [4:0] rowPos,
  output [7:0] r2,
  output [7:0] r1
);

  wire and_2_out, cdm_8_mark5_1_data_inst, cdm_8_mark5_1_mem_cycle, clk, comparator_1_eq, comparator_1_gt,
       counter_1_carry, decoder_1_out0, decoder_1_out1, IAck, IOsel, IRQ, not_1_out, not_2_out, not_3_out,
       or_1_out, READwrite, xor_1_out;
  wire [2:0] vec;
  wire [3:0] IOaddr;
  wire [7:0] bit_extender_1_out, cdm_8_mark5_1_data_out, cdm_8_mark5_1_pc, cdm_8_mark5_1_ps,
       cdm_8_mark5_1_r3, cdm_8_mark5_1_sp, controlled_buffer_2_out, IOdat, r0, random_1_out;
  wire [7:4] cdm_8_mark5_1_addr;

  Clock clock_1 (.out(clk));
  // Probe on cdm_8_mark5_1_r3
  // Probe on r2
  // Probe on r1
  // Probe on r0
  // Probe on cdm_8_mark5_1_pc
  and and_1 (IOsel, cdm_8_mark5_1_addr[4], cdm_8_mark5_1_addr[5], cdm_8_mark5_1_addr[6], cdm_8_mark5_1_addr[7], decoder_1_out1);
  // Probe on cdm_8_mark5_1_sp
  // Probe on cdm_8_mark5_1_ps
  CdM_8_mark5 cdm_8_mark5_1 (
    .clock(clk), .addr({cdm_8_mark5_1_addr, IOaddr}), .mem_read(READwrite),
    .mem_cycle(cdm_8_mark5_1_mem_cycle), .data_inst(cdm_8_mark5_1_data_inst),
    .data_out(cdm_8_mark5_1_data_out), .data_in(controlled_buffer_2_out), .r0(r0), .r1(r1), .r2(r2),
    .r3(cdm_8_mark5_1_r3), .PC(cdm_8_mark5_1_pc), .SP(cdm_8_mark5_1_sp), .PS(cdm_8_mark5_1_ps), .IAck(IAck),
    .IRQ(IRQ), .vec(vec));
  Decoder #(.disabled(0)) decoder_1 (
    .out0(decoder_1_out0), .out1(decoder_1_out1), .sel(cdm_8_mark5_1_data_inst), .en(cdm_8_mark5_1_mem_cycle));
  not not_1 (not_1_out, READwrite);
  assign IOdat = not_1_out ? cdm_8_mark5_1_data_out : 8'bz;  // Controlled_Buffer controlled_buffer_1
  assign controlled_buffer_2_out = READwrite ? IOdat : 8'bz;  // Controlled_Buffer controlled_buffer_2
  // Probe on {cdm_8_mark5_1_addr, IOaddr}
  and and_2 (and_2_out, decoder_1_out1, ~IOsel);  // AND_Gate
  not not_2 (not_2_out, clk);
  // Probe on IOdat
  RAM ram_1 (
    .addr({cdm_8_mark5_1_addr, IOaddr}), .data(IOdat), .sel(and_2_out), .clk(not_2_out), .ld(READwrite));  // open: clr
  ROM rom_1 (.addr({cdm_8_mark5_1_addr, IOaddr}), .data(IOdat), .sel(decoder_1_out0));
  assign bit_extender_1_out = {{3{1'b0}}, rowPos};  // Bit_Extender bit_extender_1
  Random random_1 (.clk(clk), .next(IOsel), .out(random_1_out));  // open: clr
  Pull_Resistor pull_resistor_1 (.node(IRQ));
  Multiplexer #(.select(4), .width(8)) multiplexer_1 (
    .in0(bit_extender_1_out), .in1(random_1_out), .out(IOdat), .sel(IOaddr), .en(IOsel));  // open: in2, in3, in4, in5, in6, in7, in8, in9, in10, in11, in12, in13, in14, in15
  assign vec = jumpInter ? 3'b001 : 3'bz;  // Controlled_Buffer controlled_buffer_3
  assign IRQ = not_3_out ? jumpInter : 1'bz;  // Controlled_Buffer controlled_buffer_4
  not not_3 (not_3_out, counter_1_carry);
  or or_1 (or_1_out, xor_1_out, comparator_1_eq);
  xor xor_1 (xor_1_out, jumpInter, comparator_1_gt);
  Counter #(.width(1), .max('h1)) counter_1 (.carry(counter_1_carry), .clk(or_1_out));  // open: load, D, count, Q, clr
  Comparator comparator_1 (.a(8'ha), .b(r0), .gt(comparator_1_gt), .eq(comparator_1_eq));  // open: lt

  // Notes on the sheet:
  //   contents of rom_1 (hex, n*v repeats v):
  //   cd f0 d3 9 c3 d3 80 c3 d9 cd 0 d5 d3 f0 bf d0 b 7c e4 1a d1 0 d2 7 ee 2b d d2 3 76 ec 26 d1 7 d2 0
  //   ee 2b 31 d2 7 36 86 d0 0 ee b 195*0 c b
endmodule

// moveChip
module movement (
  input  [7:0] movement,
  input  collision,
  input  clock,
  output isMoving
);

  wire and_1_out, comparator_1_gt, xor_1_out;
  wire [4:0] bit_extender_1_out, multiplexer_1_out, register_1_q, subtractor_1_out;

  Bit_Extender #(.out_width(5)) bit_extender_1 (.in(movement), .out(bit_extender_1_out));
  and and_1 (and_1_out, isMoving, collision);
  Multiplexer #(.width(5), .enable("false")) multiplexer_1 (
    .in0(subtractor_1_out), .in1(bit_extender_1_out), .out(multiplexer_1_out), .sel(xor_1_out));
  xor xor_1 (xor_1_out, and_1_out, collision);
  Register #(.width(5)) register_1 (.D(multiplexer_1_out), .Q(register_1_q), .clk(clock));  // open: en, clr
  _5BitOr u_5bitor_1 (.num(register_1_q), .out(isMoving));
  Subtractor #(.width(5)) subtractor_1 (
    .a(register_1_q), .b({5{1'b0}}), .out(subtractor_1_out), .bin(comparator_1_gt));  // open: bout
  Comparator #(.width(5)) comparator_1 (.a(register_1_q), .b({5{1'b0}}), .gt(comparator_1_gt));  // open: eq, lt
endmodule

// randNum
module getRandom (
  input  clock,
  output [4:0] bus_0
);

  wire comparator_1_lt;
  wire [4:0] random_1_out;

  Random #(.width(5)) random_1 (.clk(clock), .out(random_1_out));  // open: next, clr
  Comparator #(.width(5), .mode("unsigned")) comparator_1 (
    .a(random_1_out), .b(5'b10101), .lt(comparator_1_lt));  // open: gt, eq
  Register #(.width(5)) register_1 (.D(random_1_out), .Q(bus_0), .clk(comparator_1_lt));  // open: en, clr
endmodule

module keyboard (
);

  wire clock_1_out, left, right;
  wire [6:0] keyboard_1_data;

  Keyboard keyboard_1 (.clk(clock_1_out), .clr(clock_1_out), .data(keyboard_1_data));  // open: re, avail
  Clock clock_1 (.out(clock_1_out));
  Comparator #(.width(7)) comparator_1 (.a(7'b1100001), .b(keyboard_1_data), .eq(left));  // open: gt, lt
  Comparator #(.width(7)) comparator_2 (.a(keyboard_1_data), .b(7'b1100100), .eq(right));  // open: gt, lt
endmodule

module doodler (
  input  [4:0] rowPos
);

  wire [23:0] row1, row1_0, row2, row3, row4, row5, row6, row7, row8, row9, row10, row11, row12, row13,
       row14, row15, row16, row17, row18, row19, row20, row21, row22, row23, row24, row25, row26, row27,
       row28, row29, row30, row31, undriven;

  Demultiplexer #(.select(5), .width(24), .enable("false")) demultiplexer_1 (
    .out0(row1_0), .out1(row1), .out2(row2), .out3(row3), .out4(row4), .out5(row5), .out6(row6), .out7(row7),
    .out8(row8), .out9(row9), .out10(row10), .out11(row11), .out12(row12), .out13(row13), .out14(row14),
    .out15(row15), .out16(row16), .out17(row17), .out18(row18), .out19(row19), .out20(row20), .out21(row21),
    .out22(row22), .out23(row23), .out24(row24), .out25(row25), .out26(row26), .out27(row27), .out28(row28),
    .out29(row29), .out30(row30), .out31(row31), .in(undriven), .sel(rowPos));
endmodule
